# Fritzing sketch Breadboard (saved by Fritzing 1.0.6)
circuit board: 5cm x 5cm
perfboards: 1

parts:
  R4 = Resistor [tolerance=±5% power=0.25W resistance=1k package=THT]
  R2 = Resistor [tolerance=±5% power=0.25W resistance=10k package=THT]
  U1_1 = Quad Linear comparator [part_number=339 package="DIP (Dual Inline) [THT]"]
  R1 = Resistor [tolerance=±5% power=0.25W resistance=10k package=THT]
  U1_3 = Quad Linear comparator [part_number=339 package="DIP (Dual Inline) [THT]"]  # not connected
  Part1 = Quad Linear comparator [part_number=339 package="DIP (Dual Inline) [THT]"]  # not connected
  U1_4 = Quad Linear comparator [part_number=339 package="DIP (Dual Inline) [THT]"]
  R6 = Resistor [tolerance=±5% power=0.25W resistance=10k package=THT]
  U1_2 = Quad Linear comparator [part_number=339 package="DIP (Dual Inline) [THT]"]
  JP1_-_ESP32 = Header 4 [package=molex-1x4_lock]
  R5 = Resistor [tolerance=±5% power=0.25W resistance=10k package=THT]
  JP2_-_OBD = Header 3 [package=molex-1x3_lock]
  R3 = Resistor [tolerance=±5% power=0.25W resistance=6.8k package=THT]
  U1 = Quad Linear comparator [part_number=339 package="DIP (Dual Inline) [THT]"]

nets:
  N1: R4.Pin_0, JP2_-_OBD.2, U1.connector0, U1.connector6
  N2: R4.Pin_1, U1_1.VCC, R5.Pin_0, JP2_-_OBD.1, U1.connector2
  N3: R2.Pin_1, R1.Pin_1, U1_2.1IN-
  N4: U1_1.2OUT, JP1_-_ESP32.2, R3.Pin_1, U1.connector1
  N5: R1.Pin_0, JP1_-_ESP32.1, R3.Pin_0
  GND: U1_4.GND, R6.Pin_1, JP1_-_ESP32.4, JP2_-_OBD.3, U1.connector11
  N6: R6.Pin_0, R5.Pin_1, U1.connector5
  N7: JP1_-_ESP32.3, U1.connector4

notes:
  MaMUT
  12V - KLine - GND
  GND - TX - RX - VCC

custom parts:
  Quad Linear comparator: 339 quad linear comparator
  Quad Linear comparator: 339 quad linear comparator
  Quad Linear comparator: 339 quad linear comparator
  Quad Linear comparator: 339 quad linear comparator
  Quad Linear comparator: 339 quad linear comparator
  Quad Linear comparator: 339 quad linear comparator
